# Fritzing sketch Diagrama_sensor_lcd (saved by Fritzing 0.9.3b)

parts:
  S1 = KY-026
  Part1 = Arduino Uno (Rev3)
  LCD2004-I2C1 = LCD2004-I2C

nets:
  N1: S1.pin1, Part1.A3
  GND: S1.pin2, Part1.GND, LCD2004-I2C1.GND
  5V: S1.pin3, Part1.5V, LCD2004-I2C1.VCC
  N2: S1.pin4, Part1.D2
  N3: Part1.A4/SDA, LCD2004-I2C1.SDA
  N4: Part1.A5/SCL, LCD2004-I2C1.SCL

custom parts:
  KY-026: ky-026 flame sensor module
  LCD2004-I2C: A standard character display with 4x20 characters. Comes in many colors with LCM2004 IIC attached.
